// Logisim project CPU-Final-6.3 (2).circ as structural Verilog: 1 circuit, main circuit main
module main (
  input  PC_Enable,
  output END
);

  wire add_out, and_1_out, and_2_out, and_3_out, and_4_out, and_5_out, and_6_out, and_7_out, and_8_out,
       and_9_out, and_10_out, and_11_out, clock_1_out, clock_2_out, comparator_1_eq, counter_1_q, idm_out,
       idr_out, irmov_out, jmp_out, JZ_2_out, JZ_or_JMP_out, jz_out, mul_out, multiplexer_28_out,
       multiplexer_30_out, Mux_contorl_2_out, Mux_contorl_3_out, Mux_contorl_4_out, MUX_contorl_5_out,
       Mux_contorl_out, Mux_enable_2_out, Mux_enable_3_out, MUX_enable_out, nand_1_out, nand_2_out,
       nand_3_out, not_1_out, not_2_out, not_3_out, or_1_out, or_2_out, or_3_out, or_4_out, or_5_out,
       or_6_out, or_7_out, or_8_out, or_9_out, or_10_out, or_11_out, or_12_out, or_13_out, or_14_out,
       or_15_out, or_16_out, register_3_q, rrmov_out, s_r_ff_1_q, stm_out, str_out, sub_out,
       WriteBack_Enable_out, xor_1_out;
  wire [2:0] multiplexer_9_out, multiplexer_10_out, multiplexer_24_out;
  wire [3:0] multiplexer_6_out;
  wire [7:0] adder_1_out, adder_2_out, counter_2_q, demultiplexer_2_out0, demultiplexer_2_out1,
       demultiplexer_2_out2, demultiplexer_2_out3, demultiplexer_2_out4, demultiplexer_2_out5,
       demultiplexer_2_out6, demultiplexer_2_out7, eax_q, ebp_q, ebx_q, ecx_q, edi_q, edx_q, esi_q, esp_q,
       multiplexer_1_out, multiplexer_2_out, multiplexer_3_out, multiplexer_4_out, multiplexer_5_out,
       multiplexer_7_out, multiplexer_8_out, multiplexer_11_out, multiplexer_12_out, multiplexer_13_out,
       multiplexer_14_out, multiplexer_15_out, multiplexer_16_out, multiplexer_17_out, multiplexer_18_out,
       multiplexer_19_out, multiplexer_20_out, multiplexer_21_out, multiplexer_22_out, multiplexer_23_out,
       multiplexer_25_out, multiplexer_26_out, multiplexer_27_out, multiplexer_29_out, multiplexer_31_out,
       multiplier_1_out, PC_q, register_1_q_2, register_2_q, subtractor_1_out;
  wire [7:3] multiplexer_9_out_2, multiplexer_10_out_2, multiplexer_24_out_2;
  wire [19:0] controlled_buffer_1_out, controlled_buffer_2_out, demultiplexer_1_out0, demultiplexer_1_out1,
       rom_1_data;
  wire [19:8] register_1_q;

  nand nand_1 (nand_1_out, ~register_1_q[19], register_1_q[18], ~register_1_q[17], register_1_q[16]);  // NAND_Gate
  nand nand_2 (nand_2_out, register_1_q[19], ~register_1_q[18], register_1_q[17], register_1_q[16]);  // NAND_Gate
  Counter #(.width(1), .max('h1), .ongoal("stay")) counter_1 (
    .load(or_6_out), .D(or_6_out), .count(1'b0), .Q(counter_1_q), .clk(clock_1_out), .clr(and_1_out));  // open: carry
  and and_1 (and_1_out, clock_1_out, xor_1_out);
  Clock clock_1 (.out(clock_1_out));
  and and_2 (and_2_out, nand_3_out, and_3_out);
  and and_3 (and_3_out, nand_1_out, nand_2_out);
  xor xor_1 (xor_1_out, counter_1_q, or_6_out);
  and and_4 (and_4_out, ~xor_1_out, ~and_3_out);  // AND_Gate
  or or_1 (or_1_out, and_2_out, and_4_out);
  assign controlled_buffer_1_out = or_1_out ? demultiplexer_1_out0 : 20'bz;  // Controlled_Buffer controlled_buffer_1
  assign controlled_buffer_2_out = not_1_out ? rom_1_data : 20'bz;  // Controlled_Buffer controlled_buffer_2
  and and_5 (and_5_out, and_9_out, clock_2_out);
  not not_1 (not_1_out, and_9_out);
  and and_6 (and_6_out, ~register_1_q[19], ~register_1_q[18], ~multiplexer_28_out, register_1_q[17], register_1_q[16]);  // AND_Gate
  and and_7 (and_7_out, ~register_1_q[19], register_1_q[18], ~multiplexer_28_out, ~register_1_q[17], ~register_1_q[16]);  // AND_Gate
  or or_2 (or_2_out, xor_1_out, not_1_out);
  Multiplexer #(.width(8), .enable("false")) multiplexer_1 (
    .in0(PC_q), .in1(counter_2_q), .out(multiplexer_1_out), .sel(not_1_out));
  nand nand_3 (nand_3_out, ~register_1_q[19], ~register_1_q[18], ~multiplexer_28_out, register_1_q[17], register_1_q[16]);  // NAND_Gate
  Register #(.width(20), .trigger("high")) register_1 (
    .D(controlled_buffer_1_out), .Q({register_1_q, register_1_q_2}), .clk(and_5_out));  // open: en, clr
  Counter counter_2 (.Q(counter_2_q), .clk(and_8_out));  // open: load, D, count, carry, clr
  and and_8 (and_8_out, clock_2_out, ~and_9_out);  // AND_Gate
  and sub (sub_out, multiplexer_6_out[3], multiplexer_6_out[2], ~multiplexer_6_out[1], ~multiplexer_6_out[0]);  // AND_Gate
  and stm (stm_out, multiplexer_6_out[3], ~multiplexer_6_out[2], multiplexer_6_out[1], multiplexer_6_out[0]);  // AND_Gate
  and halt (END, multiplexer_6_out[3], ~multiplexer_6_out[2], multiplexer_6_out[1], ~multiplexer_6_out[0]);  // AND_Gate
  and jz (jz_out, multiplexer_6_out[3], ~multiplexer_6_out[2], ~multiplexer_6_out[1], multiplexer_6_out[0]);  // AND_Gate
  and jmp (jmp_out, multiplexer_6_out[3], ~multiplexer_6_out[2], ~multiplexer_6_out[1], ~multiplexer_6_out[0]);  // AND_Gate
  and mul (mul_out, ~multiplexer_6_out[3], multiplexer_6_out[2], multiplexer_6_out[1], multiplexer_6_out[0]);  // AND_Gate
  and add (add_out, ~multiplexer_6_out[3], multiplexer_6_out[2], multiplexer_6_out[1], ~multiplexer_6_out[0]);  // AND_Gate
  and str (str_out, ~multiplexer_6_out[3], multiplexer_6_out[2], ~multiplexer_6_out[1], multiplexer_6_out[0]);  // AND_Gate
  and idm (idm_out, ~multiplexer_6_out[3], multiplexer_6_out[2], ~multiplexer_6_out[1], ~multiplexer_6_out[0]);  // AND_Gate
  and idr (idr_out, ~multiplexer_6_out[3], ~multiplexer_6_out[2], multiplexer_6_out[1], multiplexer_6_out[0]);  // AND_Gate
  and rrmov (rrmov_out, ~multiplexer_6_out[3], ~multiplexer_6_out[2], multiplexer_6_out[1], ~multiplexer_6_out[0]);  // AND_Gate
  and irmov (irmov_out, ~multiplexer_6_out[3], ~multiplexer_6_out[2], ~multiplexer_6_out[1], multiplexer_6_out[0]);  // AND_Gate
  assign controlled_buffer_2_out = xor_1_out ? {{12{1'b0}}, multiplexer_12_out} : 20'bz;  // Controlled_Buffer controlled_buffer_3
  or or_3 (or_3_out, and_6_out, and_7_out);
  Multiplexer #(.width(8), .enable("false")) multiplexer_2 (
    .in0(multiplexer_3_out), .in1(multiplexer_18_out), .out(multiplexer_2_out), .sel(xor_1_out));
  RAM #(.dataWidth(20)) ram_1 (
    .addr(multiplexer_2_out), .data(controlled_buffer_2_out), .clk(clock_2_out), .ld(not_2_out));  // open: sel, clr
  not not_2 (not_2_out, or_2_out);
  ROM #(.dataWidth(20)) rom_1 (.addr(counter_2_q), .data(rom_1_data));  // open: sel
  or MUX_enable (MUX_enable_out, or_4_out, or_7_out, or_8_out, or_5_out, or_6_out);
  or or_4 (or_4_out, jz_out, jmp_out);
  or or_5 (or_5_out, sub_out, mul_out, add_out);
  or or_6 (or_6_out, stm_out, str_out);
  or or_7 (or_7_out, idm_out, idr_out);
  or or_8 (or_8_out, rrmov_out, irmov_out);
  Demultiplexer #(.width(20), .tristate("true"), .enable("false")) demultiplexer_1 (
    .out0(demultiplexer_1_out0), .out1(demultiplexer_1_out1), .in(controlled_buffer_2_out), .sel(or_3_out));
  Multiplexer #(.width(8), .enable("false")) multiplexer_3 (
    .in0(multiplexer_4_out), .in1(PC_q), .out(multiplexer_3_out), .sel(multiplexer_28_out));
  Multiplexer #(.select(4), .width(8), .enable("false")) multiplexer_4 (
    .in0(multiplexer_1_out), .in1(multiplexer_1_out), .in2(multiplexer_1_out), .in3(multiplexer_5_out),
    .in4(multiplexer_7_out), .in5(multiplexer_1_out), .in6(multiplexer_1_out), .in7(multiplexer_1_out),
    .in8(multiplexer_1_out), .in9(multiplexer_1_out), .in10(multiplexer_1_out), .in11(multiplexer_1_out),
    .in12(multiplexer_1_out), .in13(multiplexer_1_out), .in14(multiplexer_1_out), .in15(multiplexer_1_out),
    .out(multiplexer_4_out), .sel(register_1_q[19:16]));
  Multiplexer #(.width(8), .enable("false")) multiplexer_5 (
    .in0(multiplexer_17_out), .in1(multiplexer_1_out), .out(multiplexer_5_out), .sel(clock_2_out));
  and and_9 (and_9_out, rom_1_data[16], rom_1_data[17], rom_1_data[18], rom_1_data[19]);
  Multiplexer #(.width(4), .enable("false")) multiplexer_6 (
    .in0(4'b0000), .in1(register_1_q[19:16]), .out(multiplexer_6_out), .sel(and_9_out));
  Multiplexer #(.width(8), .enable("false")) multiplexer_7 (
    .in0(register_1_q[15:8]), .in1(multiplexer_1_out), .out(multiplexer_7_out), .sel(clock_2_out));
  or or_9 (or_9_out, or_6_out, or_5_out, or_8_out, or_7_out);
  Multiplexer #(.width(8), .enable("false")) multiplexer_8 (
    .in1(multiplexer_11_out), .out(multiplexer_8_out), .sel(and_9_out));  // open: in0
  Multiplexer #(.select(4), .width(8), .enable("false")) multiplexer_9 (
    .in2(register_1_q[15:8]), .in3(register_1_q[15:8]), .in5(register_1_q[15:8]), .in6(register_1_q[15:8]),
    .in7(register_1_q[15:8]), .in11(register_1_q[15:8]), .in12(register_1_q[15:8]),
    .out({multiplexer_9_out_2, multiplexer_9_out}), .sel(register_1_q[19:16]));  // open: in0, in1, in4, in8, in9, in10, in13, in14, in15
  Multiplexer #(.select(4), .width(8), .enable("false")) multiplexer_10 (
    .in5(register_1_q_2), .in6(register_1_q_2), .in7(register_1_q_2), .in12(register_1_q_2),
    .out({multiplexer_10_out_2, multiplexer_10_out}), .sel(register_1_q[19:16]));  // open: in0, in1, in2, in3, in4, in8, in9, in10, in11, in13, in14, in15
  Clock clock_2 (.out(clock_2_out));
  not not_3 (not_3_out, or_6_out);
  or or_10 (or_10_out, or_8_out, or_7_out);
  or or_11 (or_11_out, or_6_out, add_out);
  or or_12 (or_12_out, add_out, or_7_out, or_8_out);
  Multiplexer #(.select(4), .width(8), .enable("false")) multiplexer_11 (
    .in1(register_1_q[15:8]), .in2(multiplexer_17_out), .in3(demultiplexer_1_out1[7:0]),
    .in4(demultiplexer_1_out1[7:0]), .in5(multiplexer_17_out), .in6(multiplexer_17_out),
    .in7(multiplexer_17_out), .in8(register_1_q[15:8]), .in9(register_1_q[15:8]), .in11(multiplexer_17_out),
    .in12(multiplexer_17_out), .out(multiplexer_11_out), .sel(register_1_q[19:16]));  // open: in0, in10, in13, in14, in15
  Register eax (.D(demultiplexer_2_out0), .Q(eax_q), .clk(clock_2_out));  // open: en, clr
  Register ecx (.D(demultiplexer_2_out1), .Q(ecx_q), .clk(clock_2_out));  // open: en, clr
  or or_13 (or_13_out, and_8_out, multiplexer_28_out);
  Multiplexer #(.width(8)) multiplexer_12 (
    .in0(multiplexer_8_out), .in1(multiplexer_21_out), .out(multiplexer_12_out), .sel(not_3_out),
    .en(or_6_out));
  and Mux_contorl (Mux_contorl_out, or_10_out, ~or_11_out);  // AND_Gate
  and Mux_contorl_2 (Mux_contorl_2_out, or_6_out, ~or_12_out);  // AND_Gate
  or Mux_enable_2 (Mux_enable_2_out, mul_out, sub_out);
  Register edx (.D(demultiplexer_2_out2), .Q(edx_q), .clk(clock_2_out));  // open: en, clr
  Counter PC (
    .load(multiplexer_28_out), .D(multiplexer_26_out), .count(1'b0), .Q(PC_q), .clk(multiplexer_28_out));  // open: carry, clr
  Counter Cycle_Count (.clk(or_13_out));  // open: load, D, count, Q, carry, clr
  Multiplexer #(.width(8), .enable("false")) multiplexer_13 (
    .in0(multiplexer_15_out), .in1({8{1'b0}}), .out(multiplexer_13_out), .sel(Mux_contorl_out));
  Multiplexer #(.width(8), .enable("false")) multiplexer_14 (
    .in0(multiplexer_8_out), .in1({8{1'b0}}), .out(multiplexer_14_out), .sel(Mux_contorl_2_out));
  Multiplier multiplier_1 (.a(multiplexer_15_out), .b(multiplexer_8_out), .out(multiplier_1_out));  // open: cin, cout
  Subtractor subtractor_1 (.a(multiplexer_8_out), .b(multiplexer_15_out), .out(subtractor_1_out));  // open: bin, bout
  and Mux_contorl_3 (Mux_contorl_3_out, ~mul_out, sub_out);  // AND_Gate
  or WriteBack_Enable (WriteBack_Enable_out, or_7_out, or_8_out);
  or or_14 (or_14_out, or_7_out, or_8_out);
  Multiplexer #(.width(8), .enable("false")) multiplexer_15 (
    .in1(multiplexer_16_out), .out(multiplexer_15_out), .sel(and_9_out));  // open: in0
  Multiplexer #(.select(4), .width(8), .enable("false")) multiplexer_16 (
    .in1(register_1_q_2), .in2(register_1_q_2), .in3(register_1_q_2), .in4(register_1_q_2),
    .in5(multiplexer_25_out), .in6(multiplexer_25_out), .in7(multiplexer_25_out), .in11(register_1_q_2),
    .in12(multiplexer_25_out), .out(multiplexer_16_out), .sel(register_1_q[19:16]));  // open: in0, in8, in9, in10, in13, in14, in15
  Multiplexer #(.select(3), .width(8), .enable("false")) multiplexer_17 (
    .in0(eax_q), .in1(ecx_q), .in2(edx_q), .in3(ebx_q), .in4(esi_q), .in5(edi_q), .in6(esp_q), .in7(ebp_q),
    .out(multiplexer_17_out), .sel(multiplexer_9_out));
  Register ebx (.D(demultiplexer_2_out3), .Q(ebx_q), .clk(clock_2_out));  // open: en, clr
  Demultiplexer #(.select(3), .width(8), .tristate("true"), .enable("false")) demultiplexer_2 (
    .out0(demultiplexer_2_out0), .out1(demultiplexer_2_out1), .out2(demultiplexer_2_out2),
    .out3(demultiplexer_2_out3), .out4(demultiplexer_2_out4), .out5(demultiplexer_2_out5),
    .out6(demultiplexer_2_out6), .out7(demultiplexer_2_out7), .in(multiplexer_27_out),
    .sel(multiplexer_24_out));
  Multiplexer #(.width(8)) multiplexer_18 (
    .in0(multiplexer_22_out), .in1(multiplexer_21_out), .out(multiplexer_18_out), .sel(or_6_out),
    .en(or_6_out));
  Adder adder_1 (.a(multiplexer_13_out), .b(multiplexer_14_out), .out(adder_1_out));  // open: cin, cout
  Multiplexer #(.width(8)) multiplexer_19 (
    .in0(multiplier_1_out), .in1(subtractor_1_out), .out(multiplexer_19_out), .sel(Mux_contorl_3_out),
    .en(Mux_enable_2_out));
  Multiplexer #(.width(8)) multiplexer_20 (
    .in0(multiplexer_8_out), .in1(multiplexer_15_out), .out(multiplexer_20_out), .sel(or_14_out),
    .en(WriteBack_Enable_out));
  Register esi (.D(demultiplexer_2_out4), .Q(esi_q), .clk(clock_2_out));  // open: en, clr
  Register edi (.D(demultiplexer_2_out5), .Q(edi_q), .clk(clock_2_out));  // open: en, clr
  Multiplexer #(.width(8)) multiplexer_21 (
    .in0(adder_1_out), .in1(multiplexer_19_out), .out(multiplexer_21_out), .sel(Mux_contorl_4_out),
    .en(Mux_enable_3_out));
  or or_15 (or_15_out, or_7_out, or_8_out, add_out);
  Register esp (.D(demultiplexer_2_out6), .Q(esp_q), .clk(clock_2_out));  // open: en, clr
  and Mux_contorl_4 (Mux_contorl_4_out, ~or_15_out, Mux_enable_2_out);  // AND_Gate
  or Mux_enable_3 (Mux_enable_3_out, add_out, or_8_out, or_6_out, or_7_out, Mux_enable_2_out);
  or or_16 (or_16_out, WriteBack_Enable_out, or_5_out);
  and and_10 (and_10_out, ~or_5_out, WriteBack_Enable_out);  // AND_Gate
  Multiplexer #(.width(8), .enable("false")) multiplexer_22 (
    .in1(multiplexer_23_out), .out(multiplexer_22_out), .sel(and_9_out));  // open: in0
  Multiplexer #(.select(4), .width(8), .enable("false")) multiplexer_23 (
    .in6(register_1_q_2), .in7(register_1_q_2), .in12(register_1_q_2), .out(multiplexer_23_out),
    .sel(register_1_q[19:16]));  // open: in0, in1, in2, in3, in4, in5, in8, in9, in10, in11, in13, in14, in15
  Register ebp (.D(demultiplexer_2_out7), .Q(ebp_q), .clk(clock_2_out));  // open: en, clr
  Register register_2 (.D(multiplexer_21_out), .Q(register_2_q), .clk(clock_2_out));  // open: en, clr
  Multiplexer #(.width(8)) multiplexer_24 (
    .in0(multiplexer_22_out), .in1(multiplexer_20_out), .out({multiplexer_24_out_2, multiplexer_24_out}),
    .sel(and_10_out), .en(or_16_out));
  Multiplexer #(.select(3), .width(8), .enable("false")) multiplexer_25 (
    .in0(eax_q), .in1(ecx_q), .in2(edx_q), .in3(ebx_q), .in4(esi_q), .in5(edi_q), .in6(esp_q), .in7(ebp_q),
    .out(multiplexer_25_out), .sel(multiplexer_10_out));
  Adder adder_2 (.a(PC_q), .b(8'h1), .out(adder_2_out));  // open: cin, cout
  Comparator comparator_1 (.a(register_2_q), .b({8{1'b0}}), .eq(comparator_1_eq));  // open: gt, lt
  Multiplexer #(.width(8)) multiplexer_26 (
    .in0(multiplexer_29_out), .in1(multiplexer_8_out), .out(multiplexer_26_out), .sel(MUX_contorl_5_out),
    .en(MUX_enable_out));
  Multiplexer #(.width(8), .enable("false")) multiplexer_27 (
    .in1(multiplexer_21_out), .out(multiplexer_27_out), .sel(or_16_out));  // open: in0
  and and_11 (and_11_out, s_r_ff_1_q, register_3_q);
  Multiplexer #(.enable("false")) multiplexer_28 (
    .in0(PC_Enable), .in1(multiplexer_30_out), .out(multiplexer_28_out), .sel(and_11_out));
  Multiplexer #(.select(4), .width(8), .enable("false")) multiplexer_29 (
    .in0(PC_q), .in1(adder_2_out), .in2(adder_2_out), .in3(multiplexer_31_out), .in4(multiplexer_31_out),
    .in5(adder_2_out), .in6(adder_2_out), .in7(adder_2_out), .in8(adder_2_out), .in9(adder_2_out),
    .in10(adder_2_out), .in11(multiplexer_31_out), .in12(adder_2_out), .in13(adder_2_out),
    .in14(adder_2_out), .in15(adder_2_out), .out(multiplexer_29_out), .sel(multiplexer_6_out));
  and MUX_contorl_5 (MUX_contorl_5_out, ~or_9_out, JZ_or_JMP_out);  // AND_Gate
  or JZ_or_JMP (JZ_or_JMP_out, JZ_2_out, jmp_out);
  and JZ_2 (JZ_2_out, jz_out, comparator_1_eq);
  Multiplexer #(.enable("false")) multiplexer_30 (.in0(clock_2_out), .out(multiplexer_30_out), .sel(END));  // open: in1
  Multiplexer #(.width(8), .enable("false")) multiplexer_31 (
    .in0(adder_2_out), .in1(PC_q), .out(multiplexer_31_out), .sel(clock_2_out));
  S_R_Flip_Flop s_r_ff_1 (
    .S(MUX_enable_out), .clk(clock_2_out), .R(s_r_ff_1_q), .Q(s_r_ff_1_q));  // open: Qn, preset, reset, en
  Register #(.width(1)) register_3 (.D(and_9_out), .Q(register_3_q), .clk(clock_2_out));  // open: en, clr

  // Notes on the sheet:
  //   contents of rom_1 (hex, n*v repeats v):
  //   11a07 10300 20001 70001 10202 70201 60701 20002 70002 20706 60206 20100 60200 30704 30605 60405
  //   50501 10103 60306 60307 60301 20003 c0103 91900 80d00 a0000 1 2 3 4 5 6 7 8 9 1 2 3 4 5 6 7 8 9
  //   f0000
endmodule
